# Fritzing sketch airplaneLighting_circuit (saved by Fritzing 0.9.3b)

parts:
  Part1 = Arduino Nano (Rev3.0)
  U1 = Vibration Motor- ROB-08449 [package=vibe-motor-10mm]
  LED1 = LEDs [package=fkit-led-1206]
  LED2 = LEDs [package=fkit-led-1206]
  Q4 = Basic FET P-Channel [package="D2Pak [SMD]"]
  U3 = LIPO-1000mAh [package=lipo-1000]
  Part3 = Power Cell LiPo Charger/Booster
  R1 = Resistor [tolerance=±5% resistance=10k package="0603 [SMD]"]
  R2 = Resistor [tolerance=±5% resistance=10k package="0603 [SMD]"]
  R3 = Resistor [tolerance=±5% resistance=10k package="0603 [SMD]"]
  C1 = Capacitor [package=0603-cap]
  S1 = SPST Switch [package=switche-dpdt]
  JP1 = USB_MICROB_PLUG [package=micro-b-th]
  S2 = Round Pushbutton
  R4 = Resistor [tolerance=±5% resistance=10k package="0603 [SMD]"]
  R5 = Resistor [tolerance=±5% resistance=330 package="0603 [SMD]"]
  R6 = Resistor [tolerance=±5% resistance=330 package="0603 [SMD]"]
  Q2 = Basic FET N-Channel [package="DPak [SMD]"]
  R7 = Resistor [tolerance=±5% resistance=330 package="0603 [SMD]"]

nets:
  N1: Part1.D1/TX, JP1.D+
  N2: Part1.D0/RX, JP1.D-
  GND: Part1.GND, U1.-, LED1.C, LED2.C, U3.-, Part3.GND, R3.Pin_1, JP1.GND, S2.leg0
  N3: Part1.D2, S2.leg1, R4.Pin_0
  N4: Part1.D4, C1.2
  N5: Part1.D7, R6.Pin_0
  N6: Part1.D8, R5.Pin_0
  N7: Part1.D9, R7.Pin_0
  N8: Part1.VIN, S1.O
  N9: Part1.5V, Part3.5VIN, R4.Pin_1, Q2.drain
  N10: Part1.A1, R2.Pin_1, R3.Pin_0
  N11: U1.+, Q2.source
  N12: LED1.A, R6.Pin_1
  N13: LED2.A, R5.Pin_1
  N14: Q4.Gate, R1.Pin_0, C1.1
  N15: Q4.drain, R2.Pin_0
  N16: Q4.source, U3.+, Part3.VBATT, R1.Pin_1
  N17: Part3.VCC, S1.P
  N18: S1.S, JP1.VCC
  N19: Q2.Gate, R7.Pin_1
